// Digital circuit mico.dig as structural Verilog
module mico (
  input  clk,
  output [31:0] display
);

  wire comparator_1_eq, display_t, halt, \reg , selB, str, wr;
  wire [1:0] prox_ip, selC;
  wire [2:0] f;
  wire [15:0] add_1_s, \instrução_d , multiplexer_1_out, multiplexer_2_out, multiplexer_3_out, register_1_q,
       ula32_1_s;
  wire [31:0] B, bitextender_1_out, bitextender_2_out, multiplexer_5_out, multiplexer_6_out, ramdualport_1_d,
       registrador_1_a_2;
  wire [31:16] \instrução_d_2 , ula32_1_s_2;

  Multiplexer #(.Bits(16)) multiplexer_1 (
    .sel(comparator_1_eq), .in_0(register_1_q), .in_1(\instrução_d ), .out(multiplexer_1_out));
  Add #(.Bits(16)) add_1 (.a(multiplexer_3_out), .b(register_1_q), .c_i(1'b0), .s(add_1_s));  // open: c_o
  Multiplexer #(.Selector_Bits(2), .Bits(16)) multiplexer_2 (
    .sel(prox_ip), .in_0(add_1_s), .in_1(\instrução_d ), .in_2(registrador_1_a_2[15:0]),
    .in_3(multiplexer_1_out), .out(multiplexer_2_out));
  Register #(.Bits(16)) register_1 (.D(multiplexer_2_out), .C(clk), .en(1'b1), .Q(register_1_q));
  ROM #(.AddrBits(16), .Bits(32)) \instrução  (.A(register_1_q), .sel(1'b1), .D({\instrução_d_2 , \instrução_d }));
  Multiplexer #(.Bits(16)) multiplexer_3 (.sel(halt), .in_0(16'h1), .in_1({16{1'b0}}), .out(multiplexer_3_out));
  BitExtender #(.inputBits(16), .outputBits(32)) bitextender_1 (.in(multiplexer_2_out), .out(bitextender_1_out));
  registrador registrador_1 (
    .c(\instrução_d_2 [19:16]), .C_2(multiplexer_6_out), .clk(clk), .b(\instrução_d_2 [23:20]),
    .a(\instrução_d_2 [27:24]), .wr(wr), .B_2(B), .A_2(registrador_1_a_2));
  ROM #(.AddrBits(4), .isProgramMemory("true"), .Bits(13)) mc (
    .A(\instrução_d_2 [31:28]), .sel(1'b1), .D({wr, halt, f, selB, selC, prox_ip, \reg , str, display_t}));
  BitExtender #(.inputBits(16), .outputBits(32)) bitextender_2 (.in(\instrução_d ), .out(bitextender_2_out));
  Comparator #(.Bits(32)) comparator_1 (.a(registrador_1_a_2), .b(B), .eq(comparator_1_eq));  // open: gt, lt
  Multiplexer #(.Bits(32)) multiplexer_4 (.sel(display_t), .in_0({32{1'b0}}), .in_1(registrador_1_a_2), .out(display));
  Multiplexer #(.Bits(32)) multiplexer_5 (.sel(selB), .in_0(B), .in_1(bitextender_2_out), .out(multiplexer_5_out));
  ula32 ula32_1 (.b(multiplexer_5_out), .a(registrador_1_a_2), .F(f), .S({ula32_1_s_2, ula32_1_s}));  // open: ov
  Multiplexer #(.Selector_Bits(2), .Bits(32)) multiplexer_6 (
    .sel(selC), .in_0({ula32_1_s_2, ula32_1_s}), .in_1(ramdualport_1_d), .in_2(bitextender_1_out),
    .in_3({32{1'b0}}), .out(multiplexer_6_out));
  RAMDualPort #(.AddrBits(16), .Bits(32)) ramdualport_1 (
    .A(ula32_1_s), .Din(B), .str(str), .C(clk), .ld(1'b1), .D(ramdualport_1_d));

  // Notes on the sheet:
  //   contents of mc (hex, n*v repeats v):
  //   0,4,c,14,1c,24,2c,34,3c,5c,64,44,2,1,9,11
endmodule
