// Digital circuit registrador.dig as structural Verilog
module registrador (
  input  [3:0] c,
  input  [31:0] C_2,
  input  clk,
  input  [3:0] b,
  input  [3:0] a,
  input  wr,
  output [31:0] B_2,
  output [31:0] A_2
);

  wire and_1_out, demultiplexer_1_out_0, demultiplexer_1_out_1, demultiplexer_1_out_2, demultiplexer_1_out_3,
       demultiplexer_1_out_4, demultiplexer_1_out_5, demultiplexer_1_out_6, demultiplexer_1_out_7,
       demultiplexer_1_out_8, demultiplexer_1_out_9, demultiplexer_1_out_10, demultiplexer_1_out_11,
       demultiplexer_1_out_12, demultiplexer_1_out_13, demultiplexer_1_out_14, demultiplexer_1_out_15;
  wire [31:0] register_1_q, register_2_q, register_3_q, register_4_q, register_5_q, register_6_q,
       register_7_q, register_8_q, register_9_q, register_10_q, register_11_q, register_12_q, register_13_q,
       register_14_q, register_15_q, register_16_q;

  and and_1 (and_1_out, 1'b1, wr);
  Demultiplexer #(.Selector_Bits(4)) demultiplexer_1 (
    .sel(c), .in(and_1_out), .out_0(demultiplexer_1_out_0), .out_1(demultiplexer_1_out_1),
    .out_2(demultiplexer_1_out_2), .out_3(demultiplexer_1_out_3), .out_4(demultiplexer_1_out_4),
    .out_5(demultiplexer_1_out_5), .out_6(demultiplexer_1_out_6), .out_7(demultiplexer_1_out_7),
    .out_8(demultiplexer_1_out_8), .out_9(demultiplexer_1_out_9), .out_10(demultiplexer_1_out_10),
    .out_11(demultiplexer_1_out_11), .out_12(demultiplexer_1_out_12), .out_13(demultiplexer_1_out_13),
    .out_14(demultiplexer_1_out_14), .out_15(demultiplexer_1_out_15));
  Register #(.Bits(32)) register_1 (.D({32{1'b0}}), .C(clk), .en(1'b0), .Q(register_1_q));
  Register #(.Bits(32)) register_2 (.D(C_2), .C(clk), .en(demultiplexer_1_out_1), .Q(register_2_q));
  Register #(.Bits(32)) register_3 (.D(C_2), .C(clk), .en(demultiplexer_1_out_2), .Q(register_3_q));
  Register #(.Bits(32)) register_4 (.D(C_2), .C(clk), .en(demultiplexer_1_out_3), .Q(register_4_q));
  Register #(.Bits(32)) register_5 (.D(C_2), .C(clk), .en(demultiplexer_1_out_4), .Q(register_5_q));
  Register #(.Bits(32)) register_6 (.D(C_2), .C(clk), .en(demultiplexer_1_out_5), .Q(register_6_q));
  Register #(.Bits(32)) register_7 (.D(C_2), .C(clk), .en(demultiplexer_1_out_6), .Q(register_7_q));
  Register #(.Bits(32)) register_8 (.D(C_2), .C(clk), .en(demultiplexer_1_out_7), .Q(register_8_q));
  Register #(.Bits(32)) register_9 (.D(C_2), .C(clk), .en(demultiplexer_1_out_8), .Q(register_9_q));
  Register #(.Bits(32)) register_10 (.D(C_2), .C(clk), .en(demultiplexer_1_out_9), .Q(register_10_q));
  Register #(.Bits(32)) register_11 (.D(C_2), .C(clk), .en(demultiplexer_1_out_10), .Q(register_11_q));
  Register #(.Bits(32)) register_12 (.D(C_2), .C(clk), .en(demultiplexer_1_out_11), .Q(register_12_q));
  Register #(.Bits(32)) register_13 (.D(C_2), .C(clk), .en(demultiplexer_1_out_12), .Q(register_13_q));
  Register #(.Bits(32)) register_14 (.D(C_2), .C(clk), .en(demultiplexer_1_out_13), .Q(register_14_q));
  Register #(.Bits(32)) register_15 (.D(C_2), .C(clk), .en(demultiplexer_1_out_14), .Q(register_15_q));
  Register #(.Bits(32)) register_16 (.D(C_2), .C(clk), .en(demultiplexer_1_out_15), .Q(register_16_q));
  Multiplexer #(.Selector_Bits(4), .Bits(32)) multiplexer_1 (
    .sel(b), .in_0(register_1_q), .in_1(register_2_q), .in_2(register_3_q), .in_3(register_4_q),
    .in_4(register_5_q), .in_5(register_6_q), .in_6(register_7_q), .in_7(register_8_q), .in_8(register_9_q),
    .in_9(register_10_q), .in_10(register_11_q), .in_11(register_12_q), .in_12(register_13_q),
    .in_13(register_14_q), .in_14(register_15_q), .in_15(register_16_q), .out(B_2));
  Multiplexer #(.Selector_Bits(4), .Bits(32)) multiplexer_2 (
    .sel(a), .in_0(register_1_q), .in_1(register_2_q), .in_2(register_3_q), .in_3(register_4_q),
    .in_4(register_5_q), .in_5(register_6_q), .in_6(register_7_q), .in_7(register_8_q), .in_8(register_9_q),
    .in_9(register_10_q), .in_10(register_11_q), .in_11(register_12_q), .in_12(register_13_q),
    .in_13(register_14_q), .in_14(register_15_q), .in_15(register_16_q), .out(A_2));
  // also tied to GND on the sheet: demultiplexer_1_out_0
endmodule
