// Digital circuit ula32.dig as structural Verilog
module ula32 (
  input  [31:0] b,
  input  [31:0] a,
  input  [2:0] F,
  output [31:0] S,
  output ov
);

  wire comparator_1_lt, decoder_1_out_1;
  wire [31:0] add_1_s, \and , multiplexer_1_out, multiplexer_2_out, multiplexer_3_out, \not , not_1_out,
       \or , \xor ;
  wire [63:0] mul_1_mul;

  assign \or  = multiplexer_1_out | a;  // Or or_1, 32 bits wide
  assign \xor  = multiplexer_1_out ^ a;  // XOr xor_1, 32 bits wide
  assign \and  = multiplexer_1_out & a;  // And and_1, 32 bits wide
  assign not_1_out = ~b;  // Not not_1, 32 bits wide
  assign \not  = ~a;  // Not not_2, 32 bits wide
  Multiplexer #(.Bits(32)) multiplexer_1 (.sel(decoder_1_out_1), .in_0(b), .in_1(not_1_out), .out(multiplexer_1_out));
  Add #(.Bits(32)) add_1 (.a(a), .b(multiplexer_1_out), .c_i(1'b0), .s(add_1_s), .c_o(ov));
  Comparator #(.Bits(32)) comparator_1 (.a(a), .b(multiplexer_1_out), .lt(comparator_1_lt));  // open: gt, eq
  Mul #(.Bits(32)) mul_1 (.a(a), .b(multiplexer_1_out), .mul(mul_1_mul));
  Decoder #(.Selector_Bits(3)) decoder_1 (
    .sel(F), .out_1(decoder_1_out_1));  // open: out_0, out_2, out_3, out_4, out_5, out_6, out_7
  Multiplexer #(.Bits(32)) multiplexer_2 (
    .sel(1'b0), .in_0(mul_1_mul[31:0]), .in_1(mul_1_mul[63:32]), .out(multiplexer_2_out));
  Multiplexer #(.Bits(32)) multiplexer_3 (
    .sel(comparator_1_lt), .in_0({32{1'b0}}), .in_1(32'h1), .out(multiplexer_3_out));
  Multiplexer #(.Selector_Bits(3), .Bits(32)) multiplexer_4 (
    .sel(F), .in_0(add_1_s), .in_1(add_1_s), .in_2(multiplexer_2_out), .in_3(\and ), .in_4(\or ),
    .in_5(\xor ), .in_6(multiplexer_3_out), .in_7(\not ), .out(S));
endmodule
